# Fritzing sketch breadboard (saved by Fritzing 0.9.3b)
breadboards: 1

parts:
  Part1 = Arduino Uno (Rev3) - ICSP
  S2 = Round Pushbutton
  VCC1 = Battery block 9V
  PIR1 = PIR sensor

nets:
  5V: Part1.5V, PIR1.VDD
  GND: Part1.GND, VCC1.-, PIR1.GND
  N1: Part1.D2, PIR1.SIG
  N2: Part1.VIN, S2.leg0
  N3: S2.leg1, VCC1.+
