# Fritzing sketch shield_mod_v1 (saved by Fritzing 0.9.3b)

parts:
  S1 = SWITCH-DPDT [package=os]
  R2 = Resistor [tolerance=±5% resistance=10k package="0603 [SMD]"]
  Part1 = Arduino Wireless SD Shield
  R1 = Resistor [tolerance=±5% resistance=15k package="0603 [SMD]"]

nets:
  N1: S1.1, S1.6, Part1.ARDUINO-TX(1), Part1.N$64, Part1.N$100
  N2: S1.2, S1.5, Part1.ARDUINO-RX(0), Part1.N$62, Part1.N$101
  N3: S1.3, Part1.TX, Part1.N$106
  N4: S1.4, R2.Pin_1, Part1.N$76, Part1.N$135
  N5: R2.Pin_0, Part1.RX3, Part1.N$137, Part1.N$147, R1.Pin_1
  N6: Part1.GND, Part1.N$187, R1.Pin_0

custom parts:
  SWITCH-DPDT: DPDT Version of the COM-00597
